// Logisim project dulal.circ as structural Verilog
module CLP_3 (
  output Out_put_of_Ta,
  output Output_of_Tb
);

  wire clock_1_out, Qa_qn, Qb_qn, Ta_Qa_Qb_out;

  or Ta_Qa_Qb (Ta_Qa_Qb_out, Qa_qn, Output_of_Tb);
  Clock clock_1 (.out(clock_1_out));
  T_Flip_Flop Qb (.clk(clock_1_out), .T(Ta_Qa_Qb_out), .Q(Output_of_Tb), .Qn(Qb_qn));  // open: preset, reset, en
  T_Flip_Flop Qa (.clk(clock_1_out), .T(Qb_qn), .Q(Out_put_of_Ta), .Qn(Qa_qn));  // open: preset, reset, en

  // Notes on the sheet:
  //   Tb=Qb+Q'a
  //   Clock
  //   Name Pankaj Mahanto
  //   ID:213902002
  //   This time count 2
  //   Ta=Q'b
  //   Counter sequence:0->3->2->0
endmodule

// A
module _213902037 (
  output C,
  output B,
  output A
);

  wire clock_1_out, or_1_out, Tb_qn;

  Clock clock_1 (.out(clock_1_out));
  T_Flip_Flop Tc (.clk(clock_1_out), .T(or_1_out), .Q(C));  // open: Qn, preset, reset, en
  or or_1 (or_1_out, A, Tb_qn);
  T_Flip_Flop Tb (.clk(clock_1_out), .T(or_1_out), .Q(B), .Qn(Tb_qn));  // open: preset, reset, en
  T_Flip_Flop Ta (.clk(clock_1_out), .T(B), .Q(A));  // open: Qn, preset, reset, en
endmodule

module dulal (
  output out_1,
  output out_2,
  output out_3
);

  wire clock_1_out, or_1_out, Qa_qn;

  Clock clock_1 (.out(clock_1_out));
  T_Flip_Flop Qa (.clk(clock_1_out), .T(or_1_out), .Q(out_1), .Qn(Qa_qn));  // open: preset, reset, en
  or or_1 (or_1_out, out_2, Qa_qn);
  T_Flip_Flop Qb (.clk(clock_1_out), .T(out_1), .Q(out_2));  // open: Qn, preset, reset, en
  T_Flip_Flop Qc (.clk(clock_1_out), .T(or_1_out), .Q(out_3));  // open: Qn, preset, reset, en

  // Notes on the sheet:
  //   Dulal 
  //   Id 21390116
endmodule
